# Fritzing sketch Untitled Sketch 2 (saved by Fritzing 0.9.2b)
breadboards: 1
perfboards: 1

parts:
  J5 = shrouded pin header, 10 pins [form="♂ (shrouded male)"]
  J6 = female pin header, 2 pins [form="♀ (female)"]
  J7 = female pin header, 2 pins [form="♀ (female)"]
  J8 = female pin header, 2 pins [form="♀ (female)"]
  U1 = atmega328 [package=dip]  # not connected
  J9 = female pin header, 2 pins [form="♀ (female)"]  # not connected
  J10 = female pin header, 2 pins [form="♀ (female)"]  # not connected
  J11 = female pin header, 2 pins [form="♀ (female)"]  # not connected

nets:
  N1: J5.pin2, J6.pin2
  N2: J5.pin3, J7.pin1
  N3: J5.pin4, J7.pin2
  N4: J5.pin7, J8.pin2
  N5: J5.pin8, J8.pin1
  N6: J5.pin9, J6.pin1
