# Fritzing sketch Untitled Sketch 4 (saved by Fritzing 0.9.2b)
circuit board: 11.4018cm x 5.55036cm
breadboards: 1

parts:
  R1 = Resistor [tolerance=±5% resistance=220 package=THT]
  LED1 = LED - 3mm [color="Red (633nm)" package="3 mm [THT]"]
  Q1 = TRANSISTOR_NPN [package=to-92]
  LED2 = LED - 3mm [color="Red (633nm)" package="3 mm [THT]"]
  Q2 = TRANSISTOR_NPN [package=to-92]
  R2 = Resistor [tolerance=±5% resistance=220 package=THT]
  R3 = Resistor [tolerance=±5% resistance=220 package=THT]
  LED3 = LED - 3mm [color="Red (633nm)" package="3 mm [THT]"]
  Q3 = TRANSISTOR_NPN [package=to-92]
  R4 = Resistor [tolerance=±5% resistance=220 package=THT]
  LED4 = LED - 3mm [color="Red (633nm)" package="3 mm [THT]"]
  Q4 = TRANSISTOR_NPN [package=to-92]
  R5 = Resistor [tolerance=±5% resistance=220 package=THT]
  LED5 = LED - 3mm [color="Red (633nm)" package="3 mm [THT]"]
  Q5 = TRANSISTOR_NPN [package=to-92]
  R6 = Resistor [tolerance=±5% resistance=220 package=THT]
  LED6 = LED - 3mm [color="Red (633nm)" package="3 mm [THT]"]
  Q6 = TRANSISTOR_NPN [package=to-92]
  R7 = Resistor [tolerance=±5% resistance=220 package=THT]
  LED7 = LED - 3mm [color="Red (633nm)" package="3 mm [THT]"]
  Q7 = TRANSISTOR_NPN [package=to-92]
  R8 = Resistor [tolerance=±5% resistance=220 package=THT]
  LED8 = LED - 3mm [color="Red (633nm)" package="3 mm [THT]"]
  Q8 = TRANSISTOR_NPN [package=to-92]
  R9 = Resistor [tolerance=±5% resistance=220 package=THT]
  LED9 = LED - 3mm [color="Red (633nm)" package="3 mm [THT]"]
  Q9 = TRANSISTOR_NPN [package=to-92]
  R10 = Resistor [tolerance=±5% resistance=220 package=THT]
  LED10 = LED - 3mm [color="Red (633nm)" package="3 mm [THT]"]
  Q10 = TRANSISTOR_NPN [package=to-92]
  R11 = Resistor [tolerance=±5% resistance=220 package=THT]
  LED11 = LED - 3mm [color="Red (633nm)" package="3 mm [THT]"]
  Q11 = TRANSISTOR_NPN [package=to-92]
  R12 = Resistor [tolerance=±5% resistance=220 package=THT]
  LED12 = LED - 3mm [color="Red (633nm)" package="3 mm [THT]"]
  Q12 = TRANSISTOR_NPN [package=to-92]
  R13 = Resistor [tolerance=±5% resistance=220 package=THT]
  LED13 = LED - 3mm [color="Red (633nm)" package="3 mm [THT]"]
  Q13 = TRANSISTOR_NPN [package=to-92]
  R14 = Resistor [tolerance=±5% resistance=220 package=THT]
  LED14 = LED - 3mm [color="Red (633nm)" package="3 mm [THT]"]
  Q14 = TRANSISTOR_NPN [package=to-92]
  R15 = Resistor [tolerance=±5% resistance=220 package=THT]
  LED15 = LED - 3mm [color="Red (633nm)" package="3 mm [THT]"]
  Q15 = TRANSISTOR_NPN [package=to-92]
  R16 = Resistor [tolerance=±5% resistance=220 package=THT]
  LED16 = LED - 3mm [color="Red (633nm)" package="3 mm [THT]"]
  Q16 = TRANSISTOR_NPN [package=to-92]

nets:
  N1: R1.Pin_0, LED1.anode
  N2: R1.Pin_1, R2.Pin_1, R3.Pin_1, R4.Pin_1, R5.Pin_1, R6.Pin_1, R7.Pin_1, R8.Pin_1, R9.Pin_1, R10.Pin_1, R11.Pin_1, R12.Pin_1, R13.Pin_1, R14.Pin_1, R15.Pin_1, R16.Pin_1
  N3: LED1.cathode, Q1.C
  N4: Q1.E, Q2.E, Q3.E, Q4.E, Q5.E, Q6.E, Q7.E, Q8.E, Q9.E, Q10.E, Q11.E, Q12.E, Q13.E, Q14.E, Q15.E, Q16.E
  N5: LED2.cathode, Q2.C
  N6: LED2.anode, R2.Pin_0
  N7: R3.Pin_0, LED3.anode
  N8: LED3.cathode, Q3.C
  N9: R4.Pin_0, LED4.anode
  N10: LED4.cathode, Q4.C
  N11: R5.Pin_0, LED5.anode
  N12: LED5.cathode, Q5.C
  N13: R6.Pin_0, LED6.anode
  N14: LED6.cathode, Q6.C
  N15: R7.Pin_0, LED7.anode
  N16: LED7.cathode, Q7.C
  N17: R8.Pin_0, LED8.anode
  N18: LED8.cathode, Q8.C
  N19: R9.Pin_0, LED9.anode
  N20: LED9.cathode, Q9.C
  N21: R10.Pin_0, LED10.anode
  N22: LED10.cathode, Q10.C
  N23: R11.Pin_0, LED11.anode
  N24: LED11.cathode, Q11.C
  N25: R12.Pin_0, LED12.anode
  N26: LED12.cathode, Q12.C
  N27: R13.Pin_0, LED13.anode
  N28: LED13.cathode, Q13.C
  N29: R14.Pin_0, LED14.anode
  N30: LED14.cathode, Q14.C
  N31: R15.Pin_0, LED15.anode
  N32: LED15.cathode, Q15.C
  N33: R16.Pin_0, LED16.anode
  N34: LED16.cathode, Q16.C
