# Fritzing sketch atmega328p.power.supply (saved by Fritzing 0.9.2b)
circuit board: 14.1729cm x 9.20849cm
perfboards: 2

parts:
  U1 = atmega328 [package=dip]
  IC1 = L293D [package=THT]  # not connected
  J2 = shrouded pin header, 10 pins [form="♂ (shrouded male)"]
  J3 = female pin header, 2 pins [form="♀ (female)"]
  C1 = Capacitor [package=cap-pth-small-kit]
  C2 = Capacitor [package=cap-pth-small-kit]
  U2 = Voltage Regulator - Variable [package="TO220 [THT]"]
  R1 = Resistor [tolerance=±5% resistance=220 package=THT]
  LED1 = LED - 5mm [color="Red (633nm)" package="5 mm [THT]"]
  LED2 = LED - 5mm [color="Red (633nm)" package="5 mm [THT]"]
  R2 = Resistor [tolerance=±5% resistance=220 package=THT]

nets:
  N1: U1.RESET, J2.pin4
  N2: U1.VCC, J2.pin9, C2.1, U2.ADJ, LED2.anode
  N3: U1.GND, J2.pin7, J3.pin2, C1.1, C2.2, U2.OUT, R1.Pin_0, R2.Pin_0
  N4: U1.D11_(PWM), J2.pin8
  N5: U1.D12, J2.pin2
  N6: U1.D13, J2.pin3
  N7: J3.pin1, C1.2, U2.IN, LED1.anode
  N8: R1.Pin_1, LED1.cathode
  N9: LED2.cathode, R2.Pin_1
