# Fritzing sketch external.interrupt.example (saved by Fritzing 0.9.2b)
perfboards: 1
breadboards: 1

parts:
  U1 = atmega328 [package=dip]
  U2 = Voltage Regulator [package=to220-adj]
  J1 = female pin header, 2 pins [form="♀ (female)"]
  BAT1 = BC9VPC [package=bc9vpc]
  C1 = Ceramic Capacitor [capacitance=100nF package="200 mil [THT, multilayer]"]  # not connected
  C2 = Ceramic Capacitor [capacitance=100nF package="200 mil [THT, multilayer]"]  # not connected
  R1 = Resistor [tolerance=±5% resistance=220 package="2010 [SMD]"]
  S1 = Momentary Switch [package=ksa_sealed_tac_switch]
  LED1 = smd LED [color="Red (633nm)" package="0603 [SMD]"]
  R2 = Resistor [tolerance=±5% resistance=220 package="2010 [SMD]"]

nets:
  N1: U1.D3_(PWM), R1.Pin_1, S1.1, S1.3
  N2: U1.VCC, U2.OUT, R1.Pin_0
  N3: U1.GND#7, S1.2, S1.4, LED1.cathode
  N4: U1.A5, R2.Pin_0
  N5: U2.ADJ, J1.pin2, BAT1.V-
  N6: U2.IN, J1.pin1, BAT1.V+
  N7: LED1.anode, R2.Pin_1
