# Fritzing sketch isp.interface (saved by Fritzing 0.9.2b)
circuit board: 8.46667cm x 5.64444cm
perfboards: 1

parts:
  J1 = shrouded pin header, 10 pins [form="♂ (shrouded male)"]
  J2 = female pin header, 2 pins [form="♀ (female)"]
  J3 = female pin header, 2 pins [form="♀ (female)"]
  J4 = female pin header, 2 pins [form="♀ (female)"]

nets:
  N1: J1.pin2, J2.pin2
  N2: J1.pin3, J3.pin1
  N3: J1.pin4, J3.pin2
  N4: J1.pin7, J4.pin2
  N5: J1.pin8, J4.pin1
  N6: J1.pin9, J2.pin1
