# Fritzing sketch persistence.of.vision (saved by Fritzing 0.9.2b)
circuit board: 8.46667cm x 5.64444cm
breadboards: 1

parts:
  LED1 = LED - 3mm [color="Red (633nm)" package="3 mm [THT]"]
  R1 = Resistor [tolerance=±5% resistance=220 package=THT]
  Q2 = TRANSISTOR_NPN [package=to-92]
  U1 = atmega328 [package=dip]
  LED2 = LED - 3mm [color="Red (633nm)" package="3 mm [THT]"]
  Q3 = TRANSISTOR_NPN [package=to-92]
  R2 = Resistor [tolerance=±5% resistance=220 package=THT]
  LED3 = LED - 3mm [color="Red (633nm)" package="3 mm [THT]"]
  Q4 = TRANSISTOR_NPN [package=to-92]
  R3 = Resistor [tolerance=±5% resistance=220 package=THT]
  Q5 = TRANSISTOR_NPN [package=to-92]
  Q6 = TRANSISTOR_NPN [package=to-92]
  Q7 = TRANSISTOR_NPN [package=to-92]
  Q8 = TRANSISTOR_NPN [package=to-92]
  Q9 = TRANSISTOR_NPN [package=to-92]
  LED4 = LED - 3mm [color="Red (633nm)" package="3 mm [THT]"]
  LED5 = LED - 3mm [color="Red (633nm)" package="3 mm [THT]"]
  LED6 = LED - 3mm [color="Red (633nm)" package="3 mm [THT]"]
  LED7 = LED - 3mm [color="Red (633nm)" package="3 mm [THT]"]
  LED8 = LED - 3mm [color="Red (633nm)" package="3 mm [THT]"]
  R4 = Resistor [tolerance=±5% resistance=220 package=THT]
  R5 = Resistor [tolerance=±5% resistance=220 package=THT]
  R6 = Resistor [tolerance=±5% resistance=220 package=THT]
  R7 = Resistor [tolerance=±5% resistance=220 package=THT]
  R8 = Resistor [tolerance=±5% resistance=220 package=THT]
  R9 = Resistor [tolerance=±5% resistance=220 package=THT]
  R10 = Resistor [tolerance=±5% resistance=220 package=THT]
  R11 = Resistor [tolerance=±5% resistance=220 package=THT]
  R12 = Resistor [tolerance=±5% resistance=220 package=THT]
  R13 = Resistor [tolerance=±5% resistance=220 package=THT]
  R14 = Resistor [tolerance=±5% resistance=220 package=THT]
  R15 = Resistor [tolerance=±5% resistance=220 package=THT]
  R16 = Resistor [tolerance=±5% resistance=220 package=THT]
  LED9 = LED - 3mm [color="Red (633nm)" package="3 mm [THT]"]
  LED10 = LED - 3mm [color="Red (633nm)" package="3 mm [THT]"]
  LED11 = LED - 3mm [color="Red (633nm)" package="3 mm [THT]"]
  LED12 = LED - 3mm [color="Red (633nm)" package="3 mm [THT]"]
  LED13 = LED - 3mm [color="Red (633nm)" package="3 mm [THT]"]
  LED14 = LED - 3mm [color="Red (633nm)" package="3 mm [THT]"]
  LED15 = LED - 3mm [color="Red (633nm)" package="3 mm [THT]"]
  LED16 = LED - 3mm [color="Red (633nm)" package="3 mm [THT]"]
  Q10 = TRANSISTOR_NPN [package=to-92]
  Q11 = TRANSISTOR_NPN [package=to-92]
  Q12 = TRANSISTOR_NPN [package=to-92]
  Q13 = TRANSISTOR_NPN [package=to-92]
  Q14 = TRANSISTOR_NPN [package=to-92]
  Q15 = TRANSISTOR_NPN [package=to-92]
  Q16 = TRANSISTOR_NPN [package=to-92]
  Q17 = TRANSISTOR_NPN [package=to-92]

nets:
  N1: LED1.cathode, Q2.C
  N2: LED1.anode, R1.Pin_0
  N3: R1.Pin_1, R2.Pin_1, R3.Pin_1, R4.Pin_1, R5.Pin_1, R6.Pin_1, R7.Pin_1, R8.Pin_1, R9.Pin_1, R12.Pin_1, R15.Pin_1, R16.Pin_1
  N4: Q2.E, U1.GND#7, U1.D13, Q3.E, Q4.E, Q5.E, Q6.E, Q7.E, Q8.E, Q9.E, Q9.B, Q10.E, Q11.E, Q12.E, Q13.E, Q14.E, Q15.E, Q16.E, Q17.E
  N5: Q2.B, U1.D8
  N6: U1.D0_(RX), Q17.B
  N7: U1.D1_(TX), Q16.B
  N8: U1.D2, Q15.B
  N9: U1.D3_(PWM), Q14.B
  N10: U1.D4, Q13.B
  N11: U1.XLAT1, Q8.B
  N12: U1.D5_(PWM), Q12.B
  N13: U1.D6_(PWM), Q11.B
  N14: U1.D7, Q10.B
  N15: U1.D9_(PWM), Q3.B
  N16: U1.D10_(PWM), Q4.B
  N17: U1.D11_(PWM), Q6.B
  N18: U1.D12, Q5.B
  N19: LED2.cathode, Q3.C
  N20: LED2.anode, R2.Pin_0
  N21: LED3.cathode, Q4.C
  N22: LED3.anode, R3.Pin_0
  N23: Q5.C, LED5.cathode
  N24: Q6.C, LED4.cathode
  N25: Q7.C, LED6.cathode
  N26: Q8.C, LED7.cathode
  N27: Q9.C, LED8.cathode
  N28: LED4.anode, R4.Pin_0
  N29: LED5.anode, R5.Pin_0
  N30: LED6.anode, R6.Pin_0
  N31: LED7.anode, R7.Pin_0
  N32: LED8.anode, R8.Pin_0
  N33: R9.Pin_0, LED16.anode
  N34: R10.Pin_0, LED14.anode
  N35: R11.Pin_0, LED12.anode
  N36: R12.Pin_0, LED15.anode
  N37: R13.Pin_0, LED9.anode
  N38: R14.Pin_0, LED11.anode
  N39: R15.Pin_0, LED13.anode
  N40: R16.Pin_0, LED10.anode
  N41: LED9.cathode, Q12.C
  N42: LED10.cathode, Q17.C
  N43: LED11.cathode, Q14.C
  N44: LED12.cathode, Q16.C
  N45: LED13.cathode, Q11.C
  N46: LED14.cathode, Q10.C
  N47: LED15.cathode, Q15.C
  N48: LED16.cathode, Q13.C
